// Logisim project gpu32.circ as structural Verilog: 15 circuits, main circuit main
module main (
);

  wire clock_1_out, Reset_out;

  Clock clock_1 (.out(clock_1_out));
  Button Reset (.out(Reset_out));
  G32 g32_1 (.clk(clock_1_out), .reset(Reset_out), .en(1'b1));
endmodule

module G32 (
  input  clk,
  input  reset,
  input  en
);

  wire g32_id_1_alu_is_lea, g32_id_1_alu_sel_imm, g32_id_1_ldr_ram, g32_id_1_ra_is_rd, g32_id_1_rf_wb,
       g32_memc_1_lds_ack_2, g32_memc_1_lds_stall, g32_memc_1_lds_stall_2, g32_memc_1_lds_stall_3,
       g32_memc_1_lds_stb_5, g32_memc_1_lds_wr_5, g32_memc_1_ram_ack_2, g32_memc_1_ram_stall,
       g32_memc_1_ram_stall_2, g32_memc_1_ram_stall_3, g32_memc_1_ram_stb_5, g32_memc_1_ram_wr_5,
       g32_thread_1_lds_stb, g32_thread_1_lds_wr, g32_thread_1_ram_stb, g32_thread_1_ram_wr,
       g32_thread_2_lds_stb, g32_thread_2_lds_wr, g32_thread_2_ram_stb, g32_thread_2_ram_wr,
       g32_thread_3_lds_stb, g32_thread_3_lds_wr, g32_thread_3_ram_stb, g32_thread_3_ram_wr,
       g32_thread_4_lds_stb, g32_thread_4_lds_wr, g32_thread_4_ram_stb, g32_thread_4_ram_wr, register_7_q,
       register_8_q, register_10_q, register_11_q, register_20_q, register_23_q, register_24_q;
  wire [1:0] g32_thread_1_lane_id_out, g32_thread_2_lane_id_out, g32_thread_3_lane_id_out,
       pull_resistor_1_node, pull_resistor_3_node;
  wire [2:0] g32_id_pre_1_predicate, register_6_q, register_15_q, register_16_q, register_19_q, undriven;
  wire [3:0] g32_id_1_alu_cmd, pull_resistor_2_node, register_9_q;
  wire [4:0] g32_id_pre_1_ra, g32_id_pre_1_rb, g32_id_pre_1_rd, multiplexer_1_out, register_2_q,
       register_3_q, register_4_q, register_12_q, register_13_q, register_14_q;
  wire [7:0] g32_id_pre_1_opcode, g32_if_1_imem_addr, register_5_q;
  wire [9:0] g32_memc_1_lds_addr_5, g32_thread_1_lds_addr, g32_thread_2_lds_addr, g32_thread_3_lds_addr,
       g32_thread_4_lds_addr;
  wire [11:0] g32_memc_1_ram_addr_5, g32_thread_1_ram_addr, g32_thread_2_ram_addr, g32_thread_3_ram_addr,
       g32_thread_4_ram_addr, register_21_q;
  wire [11:10] register_18_q;
  wire [20:0] g32_id_pre_1_predec_instruction, register_1_q;
  wire [31:0] g32_id_1_imm, g32_memc_1_lds_din_2, g32_memc_1_lds_din_3, g32_memc_1_lds_din_4,
       g32_memc_1_lds_din_5, g32_memc_1_lds_dout_4, g32_memc_1_ram_din_2, g32_memc_1_ram_din_3,
       g32_memc_1_ram_din_4, g32_memc_1_ram_din_5, g32_memc_1_ram_dout_6, g32_thread_1_lds_dout,
       g32_thread_1_ram_dout, g32_thread_2_lds_dout, g32_thread_2_ram_dout, g32_thread_3_lds_dout,
       g32_thread_3_ram_dout, g32_thread_4_lds_dout, g32_thread_4_ram_dout, ram_1_data, ram_2_data,
       ram_3_data, register_17_q, register_22_q, register_25_q;

  G32_ID_Pre g32_id_pre_1 (
    .instruction(ram_1_data), .predec_instruction(g32_id_pre_1_predec_instruction), .rb(g32_id_pre_1_rb),
    .ra(g32_id_pre_1_ra), .rd(g32_id_pre_1_rd), .opcode(g32_id_pre_1_opcode),
    .predicate(g32_id_pre_1_predicate));
  RAM #(.dataWidth(32)) ram_1 (.addr(g32_if_1_imem_addr), .data(ram_1_data), .clk(clk));  // open: sel, ld, clr
  // Probe on g32_if_1_imem_addr
  Register #(.width(21)) register_1 (
    .D(g32_id_pre_1_predec_instruction), .en(en), .Q(register_1_q), .clk(clk), .clr(reset));
  Register #(.width(5)) register_2 (.D(g32_id_pre_1_rb), .en(en), .Q(register_2_q), .clk(clk), .clr(reset));
  Register #(.width(5)) register_3 (.D(g32_id_pre_1_ra), .en(en), .Q(register_3_q), .clk(clk), .clr(reset));
  Register #(.width(5)) register_4 (.D(g32_id_pre_1_rd), .en(en), .Q(register_4_q), .clk(clk), .clr(reset));
  Register register_5 (.D(g32_id_pre_1_opcode), .en(en), .Q(register_5_q), .clk(clk), .clr(reset));
  Register #(.width(3)) register_6 (.D(g32_id_pre_1_predicate), .en(en), .Q(register_6_q), .clk(clk), .clr(reset));
  G32_IF g32_if_1 (.imem_addr(g32_if_1_imem_addr), .clk(clk), .reset(reset), .en(en));
  // Probe on register_1_q
  // Probe on register_5_q
  G32_ID g32_id_1 (
    .predec_instruction(register_1_q), .opcode(register_5_q), .imm(g32_id_1_imm), .rf_wb(g32_id_1_rf_wb),
    .alu_cmd(g32_id_1_alu_cmd), .alu_is_lea(g32_id_1_alu_is_lea), .alu_sel_imm(g32_id_1_alu_sel_imm),
    .ldr_ram(g32_id_1_ldr_ram), .ra_is_rd(g32_id_1_ra_is_rd));
  // Probe on register_2_q
  Multiplexer #(.width(5), .disabled(0), .enable("false")) multiplexer_1 (
    .in0(register_3_q), .in1(register_4_q), .out(multiplexer_1_out), .sel(g32_id_1_ra_is_rd));
  // Probe on multiplexer_1_out
  // Probe on register_4_q
  // Probe on register_6_q
  Pull_Resistor pull_resistor_1 (.node(pull_resistor_1_node));
  // Probe on pull_resistor_1_node
  Register #(.width(1)) register_7 (.D(g32_id_1_ldr_ram), .en(en), .Q(register_7_q), .clk(clk), .clr(reset));
  Register #(.width(1)) register_8 (.D(g32_id_1_rf_wb), .en(en), .Q(register_8_q), .clk(clk), .clr(reset));
  Register #(.width(4)) register_9 (.D(g32_id_1_alu_cmd), .en(en), .Q(register_9_q), .clk(clk), .clr(reset));
  Register #(.width(1)) register_10 (.D(g32_id_1_alu_is_lea), .en(en), .Q(register_10_q), .clk(clk), .clr(reset));
  Register #(.width(1)) register_11 (.D(g32_id_1_alu_sel_imm), .en(en), .Q(register_11_q), .clk(clk), .clr(reset));
  Register #(.width(5)) register_12 (.D(register_2_q), .en(en), .Q(register_12_q), .clk(clk), .clr(reset));
  Register #(.width(5)) register_13 (.D(multiplexer_1_out), .en(en), .Q(register_13_q), .clk(clk), .clr(reset));
  Register #(.width(5)) register_14 (.D(register_4_q), .en(en), .Q(register_14_q), .clk(clk), .clr(reset));
  Register #(.width(3)) register_15 (.en(en), .Q(register_15_q), .clk(clk), .clr(reset));  // open: D
  Register #(.width(3)) register_16 (.D(register_6_q), .en(en), .Q(register_16_q), .clk(clk), .clr(reset));
  Register #(.width(32)) register_17 (.D(g32_id_1_imm), .en(en), .Q(register_17_q), .clk(clk), .clr(reset));
  Register #(.width(2)) register_18 (.D(pull_resistor_1_node), .en(en), .Q(register_18_q), .clk(clk), .clr(reset));
  Register #(.width(3)) register_19 (.D(undriven), .en(en), .Q(register_19_q), .clk(clk), .clr(reset));
  Pull_Resistor #(.pull(1)) pull_resistor_2 (.node(pull_resistor_2_node));
  // Probe on register_8_q
  // Probe on register_9_q
  // Probe on register_10_q
  // Probe on register_11_q
  // Probe on register_12_q
  // Probe on register_13_q
  // Probe on register_14_q
  // Probe on register_16_q
  // Probe on register_17_q
  // Probe on register_18_q
  // Probe on pull_resistor_2_node
  G32_THREAD g32_thread_1 (
    .clk(clk), .reset(reset), .en(pull_resistor_2_node[0]), .rd(register_14_q), .rb(register_12_q),
    .ra(register_13_q), .tid(register_18_q), .imm(register_17_q), .rf_wr(register_8_q),
    .lane_id_in(pull_resistor_3_node), .lane_id_out(g32_thread_1_lane_id_out),
    .RAM_ADDR(g32_thread_1_ram_addr), .RAM_WR(g32_thread_1_ram_wr), .RAM_DIN(g32_memc_1_ram_din_2),
    .RAM_DOUT(g32_thread_1_ram_dout), .LDS_ADDR(g32_thread_1_lds_addr), .LDS_WR(g32_thread_1_lds_wr),
    .LDS_DIN(g32_memc_1_lds_din_2), .LDS_DOUT(g32_thread_1_lds_dout), .LDS_STALL(g32_memc_1_lds_ack_2),
    .RAM_STALL(g32_memc_1_ram_ack_2), .RAM_STB(g32_thread_1_ram_stb), .LDS_STB(g32_thread_1_lds_stb),
    .predicate(register_19_q), .alu_is_lea(register_10_q), .alu_sel_imm(register_11_q),
    .alu_cmd(register_9_q), .ldr_ram(register_7_q));
  G32_THREAD g32_thread_2 (
    .clk(clk), .reset(reset), .en(pull_resistor_2_node[1]), .rd(register_14_q), .rb(register_12_q),
    .ra(register_13_q), .tid(register_18_q), .imm(register_17_q), .rf_wr(register_8_q),
    .lane_id_in(g32_thread_1_lane_id_out), .lane_id_out(g32_thread_2_lane_id_out),
    .RAM_ADDR(g32_thread_2_ram_addr), .RAM_WR(g32_thread_2_ram_wr), .RAM_DIN(g32_memc_1_ram_din_3),
    .RAM_DOUT(g32_thread_2_ram_dout), .LDS_ADDR(g32_thread_2_lds_addr), .LDS_WR(g32_thread_2_lds_wr),
    .LDS_DIN(g32_memc_1_lds_din_3), .LDS_DOUT(g32_thread_2_lds_dout), .LDS_STALL(g32_memc_1_lds_stall),
    .RAM_STALL(g32_memc_1_ram_stall), .RAM_STB(g32_thread_2_ram_stb), .LDS_STB(g32_thread_2_lds_stb),
    .predicate(register_19_q), .alu_is_lea(register_10_q), .alu_sel_imm(register_11_q),
    .alu_cmd(register_9_q), .ldr_ram(register_7_q));
  G32_THREAD g32_thread_3 (
    .clk(clk), .reset(reset), .en(pull_resistor_2_node[2]), .rd(register_14_q), .rb(register_12_q),
    .ra(register_13_q), .tid(register_18_q), .imm(register_17_q), .rf_wr(register_8_q),
    .lane_id_in(g32_thread_2_lane_id_out), .lane_id_out(g32_thread_3_lane_id_out),
    .RAM_ADDR(g32_thread_3_ram_addr), .RAM_WR(g32_thread_3_ram_wr), .RAM_DIN(g32_memc_1_ram_din_4),
    .RAM_DOUT(g32_thread_3_ram_dout), .LDS_ADDR(g32_thread_3_lds_addr), .LDS_WR(g32_thread_3_lds_wr),
    .LDS_DIN(g32_memc_1_lds_din_4), .LDS_DOUT(g32_thread_3_lds_dout), .LDS_STALL(g32_memc_1_lds_stall_2),
    .RAM_STALL(g32_memc_1_ram_stall_2), .RAM_STB(g32_thread_3_ram_stb), .LDS_STB(g32_thread_3_lds_stb),
    .predicate(register_19_q), .alu_is_lea(register_10_q), .alu_sel_imm(register_11_q),
    .alu_cmd(register_9_q), .ldr_ram(register_7_q));
  G32_THREAD g32_thread_4 (
    .clk(clk), .reset(reset), .en(pull_resistor_2_node[3]), .rd(register_14_q), .rb(register_12_q),
    .ra(register_13_q), .tid(register_18_q), .imm(register_17_q), .rf_wr(register_8_q),
    .lane_id_in(g32_thread_3_lane_id_out), .RAM_ADDR(g32_thread_4_ram_addr), .RAM_WR(g32_thread_4_ram_wr),
    .RAM_DIN(g32_memc_1_ram_din_5), .RAM_DOUT(g32_thread_4_ram_dout), .LDS_ADDR(g32_thread_4_lds_addr),
    .LDS_WR(g32_thread_4_lds_wr), .LDS_DIN(g32_memc_1_lds_din_5), .LDS_DOUT(g32_thread_4_lds_dout),
    .LDS_STALL(g32_memc_1_lds_stall_3), .RAM_STALL(g32_memc_1_ram_stall_3), .RAM_STB(g32_thread_4_ram_stb),
    .LDS_STB(g32_thread_4_lds_stb), .predicate(register_19_q), .alu_is_lea(register_10_q),
    .alu_sel_imm(register_11_q), .alu_cmd(register_9_q), .ldr_ram(register_7_q));  // open: lane_id_out
  Pull_Resistor pull_resistor_3 (.node(pull_resistor_3_node));
  // Probe on pull_resistor_3_node
  // Probe on g32_thread_1_lane_id_out
  // Probe on g32_thread_2_lane_id_out
  // Probe on g32_thread_3_lane_id_out
  G32_MEMC g32_memc_1 (
    .RAM_ACK(register_24_q), .RAM_DIN(register_25_q), .LDS_ACK(register_23_q), .LDS_DIN(ram_3_data),
    .RAM_STB_5(g32_memc_1_ram_stb_5), .RAM_WR_5(g32_memc_1_ram_wr_5), .RAM_ADDR_5(g32_memc_1_ram_addr_5),
    .RAM_DOUT_6(g32_memc_1_ram_dout_6), .LDS_STB_5(g32_memc_1_lds_stb_5), .LDS_WR_5(g32_memc_1_lds_wr_5),
    .LDS_ADDR_5(g32_memc_1_lds_addr_5), .LDS_DOUT_4(g32_memc_1_lds_dout_4), .clk(clk), .reset(reset),
    .RAM_STB(g32_thread_1_ram_stb), .RAM_WR(g32_thread_1_ram_wr), .RAM_ADDR(g32_thread_1_ram_addr),
    .RAM_ACK_2(g32_memc_1_ram_ack_2), .RAM_DIN_2(g32_memc_1_ram_din_2), .RAM_DOUT(g32_thread_1_ram_dout),
    .LDS_STB(g32_thread_1_lds_stb), .LDS_WR(g32_thread_1_lds_wr), .LDS_ADDR(g32_thread_1_lds_addr),
    .LDS_ACK_2(g32_memc_1_lds_ack_2), .LDS_DIN_2(g32_memc_1_lds_din_2), .LDS_DOUT(g32_thread_1_lds_dout),
    .RAM_STB_2(g32_thread_2_ram_stb), .RAM_WR_2(g32_thread_2_ram_wr), .RAM_ADDR_2(g32_thread_2_ram_addr),
    .RAM_STALL(g32_memc_1_ram_stall), .RAM_DIN_3(g32_memc_1_ram_din_3), .RAM_DOUT_2(g32_thread_2_ram_dout),
    .LDS_STB_2(g32_thread_2_lds_stb), .LDS_WR_2(g32_thread_2_lds_wr), .LDS_ADDR_2(g32_thread_2_lds_addr),
    .LDS_STALL(g32_memc_1_lds_stall), .LDS_DIN_3(g32_memc_1_lds_din_3), .LDS_DOUT_2(g32_thread_2_lds_dout),
    .RAM_STB_3(g32_thread_3_ram_stb), .RAM_WR_3(g32_thread_3_ram_wr), .RAM_ADDR_3(g32_thread_3_ram_addr),
    .RAM_STALL_2(g32_memc_1_ram_stall_2), .RAM_DIN_4(g32_memc_1_ram_din_4),
    .RAM_DOUT_3(g32_thread_3_ram_dout), .LDS_STB_3(g32_thread_3_lds_stb), .LDS_WR_3(g32_thread_3_lds_wr),
    .LDS_ADDR_3(g32_thread_3_lds_addr), .LDS_STALL_2(g32_memc_1_lds_stall_2),
    .LDS_DIN_4(g32_memc_1_lds_din_4), .LDS_DOUT_3(g32_thread_3_lds_dout), .RAM_STB_4(g32_thread_4_ram_stb),
    .RAM_WR_4(g32_thread_4_ram_wr), .RAM_ADDR_4(g32_thread_4_ram_addr), .RAM_STALL_3(g32_memc_1_ram_stall_3),
    .RAM_DIN_5(g32_memc_1_ram_din_5), .RAM_DOUT_4(g32_thread_4_ram_dout), .LDS_STB_4(g32_thread_4_lds_stb),
    .LDS_WR_4(g32_thread_4_lds_wr), .LDS_ADDR_4(g32_thread_4_lds_addr), .LDS_STALL_3(g32_memc_1_lds_stall_3),
    .LDS_DIN_5(g32_memc_1_lds_din_5), .RAM_DOUT_5(g32_thread_4_lds_dout));
  Register #(.width(1)) register_20 (.D(g32_memc_1_ram_stb_5), .Q(register_20_q), .clk(clk), .clr(reset));  // open: en
  Register #(.width(12)) register_21 (
    .D(g32_memc_1_ram_addr_5), .Q(register_21_q), .clk(clk), .clr(reset));  // open: en
  Register #(.width(32)) register_22 (
    .D(g32_memc_1_ram_dout_6), .Q(register_22_q), .clk(clk), .clr(reset));  // open: en
  Register #(.width(1)) register_23 (.D(g32_memc_1_lds_stb_5), .Q(register_23_q), .clk(clk), .clr(reset));  // open: en
  Register #(.width(1)) register_24 (.D(register_20_q), .Q(register_24_q), .clk(clk), .clr(reset));  // open: en
  Register #(.width(32)) register_25 (.D(ram_2_data), .Q(register_25_q), .clk(clk), .clr(reset));  // open: en
  RAM #(.addrWidth(12), .dataWidth(32), .bus("separate")) ram_2 (
    .addr(register_21_q), .din(register_22_q), .data(ram_2_data), .str(g32_memc_1_ram_wr_5), .clk(clk));  // open: sel, ld, clr
  RAM #(.addrWidth(12), .dataWidth(32), .bus("separate")) ram_3 (
    .addr({register_18_q, g32_memc_1_lds_addr_5}), .din(g32_memc_1_lds_dout_4), .data(ram_3_data),
    .str(g32_memc_1_lds_wr_5), .clk(clk));  // open: sel, ld, clr

  // Notes on the sheet:
  //   en: pull=up
  //   IMEM
  //   Missing:
  //   Immediate decoding
  //   Any jumping/branching
  //   LEA
  //   ThreadId latency incorrect for RAM/LDS
  //   See LSU UNIT
  //   Interconnect
  //   Memory I/O
  //   Flag upgate gates
  //   DMEM (RAM)
  //   DMEM (LDS)
endmodule

module G32_IF (
  input  clk,
  input  reset,
  input  en,
  output [7:0] imem_addr
);

  wire comparator_1_eq, or_1_out;
  wire [7:0] adder_1_out;

  or or_1 (or_1_out, reset, comparator_1_eq);
  Register register_1 (.D(adder_1_out), .en(en), .Q(imem_addr), .clk(clk), .clr(or_1_out));
  Adder adder_1 (.a(imem_addr), .b(8'h1), .out(adder_1_out));  // open: cin, cout
  Comparator comparator_1 (.a(imem_addr), .b(8'hb), .eq(comparator_1_eq));  // open: gt, lt
endmodule

module G32_ID_Pre (
  input  [31:0] instruction,
  output [20:0] predec_instruction,
  output [4:0] rb,
  output [4:0] ra,
  output [4:0] rd,
  output [2:0] predicate,
  output [7:0] opcode
);

  // Probe on instruction[10:6]
  // Probe on instruction[15:11]
  // Probe on instruction[20:16]

  assign opcode = instruction[31:24];
  assign predec_instruction = instruction[20:0];
  assign predicate = instruction[23:21];
  assign ra = instruction[15:11];
  assign rb = instruction[10:6];
  assign rd = instruction[20:16];
endmodule

module G32_ID (
  input  [20:0] predec_instruction,
  input  [7:0] opcode,
  output alu_is_lea,
  output alu_sel_imm,
  output [31:0] imm,
  output [3:0] alu_cmd,
  output rf_wb,
  output ra_is_rd,
  output ldr_ram
);

  wire comparator_1_eq, comparator_2_eq, comparator_3_eq, comparator_3_lt, comparator_4_eq, comparator_5_eq,
       comparator_5_lt, comparator_6_eq, or_1_out, or_3_out, or_5_out, or_6_out, pull_resistor_8_node,
       pull_resistor_9_node;
  wire [3:0] multiplexer_1_out, pull_resistor_7_node;
  wire [3:3] pull_resistor_1_node;
  wire [15:0] multiplexer_2_out, multiplexer_3_out, pull_resistor_2_node, pull_resistor_3_node;
  wire [31:0] multiplexer_4_out, pull_resistor_4_node, pull_resistor_6_node;

  // Probe on predec_instruction[15:0]
  Comparator #(.width(4)) comparator_1 (.a(opcode[7:4]), .b(4'b0000), .eq(comparator_1_eq));  // open: gt, lt
  Comparator #(.width(4)) comparator_2 (.a(opcode[7:4]), .b(4'b0001), .eq(comparator_2_eq));  // open: gt, lt
  Comparator comparator_3 (.a(opcode), .b(8'h80), .eq(comparator_3_eq), .lt(comparator_3_lt));  // open: gt
  Comparator comparator_4 (.a(opcode), .b(8'h81), .eq(comparator_4_eq));  // open: gt, lt
  Comparator comparator_5 (.a(opcode), .b(8'h84), .eq(comparator_5_eq), .lt(comparator_5_lt));  // open: gt
  Comparator comparator_6 (.a(opcode), .b(8'h85), .eq(comparator_6_eq));  // open: gt, lt
  Pull_Resistor pull_resistor_1 (.node(pull_resistor_1_node[3]));
  Pull_Resistor pull_resistor_2 (.node(pull_resistor_2_node));
  Pull_Resistor pull_resistor_3 (.node(pull_resistor_3_node));
  Multiplexer #(.width(4), .disabled(0), .enable("false")) multiplexer_1 (
    .in0({pull_resistor_1_node[3], opcode[2:0]}), .in1(opcode[3:0]), .out(multiplexer_1_out),
    .sel(comparator_1_eq));
  Multiplexer #(.width(16), .disabled(0), .enable("false")) multiplexer_2 (
    .in0(pull_resistor_2_node), .in1(predec_instruction[15:0]), .out(multiplexer_2_out), .sel(comparator_3_eq));
  Multiplexer #(.width(16), .disabled(0), .enable("false")) multiplexer_3 (
    .in0(pull_resistor_3_node), .in1(predec_instruction[15:0]), .out(multiplexer_3_out), .sel(comparator_4_eq));
  or or_1 (or_1_out, comparator_3_eq, comparator_4_eq);
  // Probe on {multiplexer_3_out, multiplexer_2_out}
  Multiplexer #(.width(32), .disabled(0), .enable("false")) multiplexer_4 (
    .in0({multiplexer_3_out, multiplexer_2_out}), .in1(pull_resistor_4_node), .out(multiplexer_4_out),
    .sel(comparator_2_eq));
  Pull_Resistor #(.pull("X")) pull_resistor_4 (.node(pull_resistor_4_node));
  or or_2 (alu_sel_imm, or_1_out, comparator_2_eq);
  or or_3 (or_3_out, comparator_1_eq, comparator_2_eq);
  or or_4 (ra_is_rd, comparator_3_eq, comparator_4_eq);
  Pull_Resistor pull_resistor_5 (.node(alu_is_lea));
  Pull_Resistor #(.pull("X")) pull_resistor_6 (.node(pull_resistor_6_node));
  Multiplexer #(.width(32), .disabled(0), .enable("false")) multiplexer_5 (
    .in0(pull_resistor_6_node), .in1(multiplexer_4_out), .out(imm), .sel(alu_sel_imm));
  Pull_Resistor pull_resistor_7 (.node(pull_resistor_7_node));
  Multiplexer #(.width(4), .disabled(0), .enable("false")) multiplexer_6 (
    .in0(pull_resistor_7_node), .in1(multiplexer_1_out), .out(alu_cmd), .sel(or_5_out));
  or or_5 (or_5_out, or_3_out, pull_resistor_8_node);
  Pull_Resistor pull_resistor_8 (.node(pull_resistor_8_node));
  or or_6 (or_6_out, or_3_out, ra_is_rd);
  Pull_Resistor pull_resistor_9 (.node(pull_resistor_9_node));
  or or_7 (rf_wb, or_6_out, comparator_5_eq, pull_resistor_9_node);
  Pull_Resistor #(.pull("X")) pull_resistor_10 (.node(ldr_ram));

  // Notes on the sheet:
  //   LLI
  //   LUI
  //   LD
  //   ST
  //   extended ALU ops restriced to not imm
  //   ALU
  //   ALUI
  //   ALU
  //   ALUI
  //   LLI
  //   LUI
  //   LD
  //   ST
endmodule

module G32_MEMC (
  input  clk,
  input  reset,
  input  RAM_STB,
  input  RAM_WR,
  input  RAM_ACK,
  input  [11:0] RAM_ADDR,
  input  [31:0] RAM_DOUT,
  input  [31:0] RAM_DIN,
  input  LDS_STB,
  input  LDS_WR,
  input  LDS_ACK,
  input  [9:0] LDS_ADDR,
  input  [31:0] LDS_DOUT,
  input  [31:0] LDS_DIN,
  input  RAM_STB_2,
  input  RAM_WR_2,
  input  [11:0] RAM_ADDR_2,
  input  [31:0] RAM_DOUT_2,
  input  LDS_STB_2,
  input  LDS_WR_2,
  input  [9:0] LDS_ADDR_2,
  input  [31:0] LDS_DOUT_2,
  input  RAM_STB_3,
  input  RAM_WR_3,
  input  [11:0] RAM_ADDR_3,
  input  [31:0] RAM_DOUT_3,
  input  LDS_STB_3,
  input  LDS_WR_3,
  input  [9:0] LDS_ADDR_3,
  input  [31:0] LDS_DOUT_3,
  input  RAM_STB_4,
  input  RAM_WR_4,
  input  [11:0] RAM_ADDR_4,
  input  [31:0] RAM_DOUT_4,
  input  LDS_STB_4,
  input  LDS_WR_4,
  input  [9:0] LDS_ADDR_4,
  input  [31:0] RAM_DOUT_5,
  output RAM_STB_5,
  output RAM_WR_5,
  output RAM_ACK_2,
  output [11:0] RAM_ADDR_5,
  output [31:0] RAM_DOUT_6,
  output [31:0] RAM_DIN_2,
  output LDS_STB_5,
  output LDS_WR_5,
  output LDS_ACK_2,
  output [9:0] LDS_ADDR_5,
  output [31:0] LDS_DOUT_4,
  output [31:0] LDS_DIN_2,
  output RAM_STALL,
  output [31:0] RAM_DIN_3,
  output LDS_STALL,
  output [31:0] LDS_DIN_3,
  output RAM_STALL_2,
  output [31:0] RAM_DIN_4,
  output LDS_STALL_2,
  output [31:0] LDS_DIN_4,
  output RAM_STALL_3,
  output [31:0] RAM_DIN_5,
  output LDS_STALL_3,
  output [31:0] LDS_DIN_5
);


  assign LDS_ACK_2 = LDS_ACK;
  assign LDS_ADDR_5 = LDS_ADDR;
  assign LDS_DIN_2 = LDS_DIN;
  assign LDS_DOUT_4 = LDS_DOUT;
  assign LDS_STB_5 = LDS_STB;
  assign LDS_WR_5 = LDS_WR;
  assign RAM_ACK_2 = RAM_ACK;
  assign RAM_ADDR_5 = RAM_ADDR;
  assign RAM_DIN_2 = RAM_DIN;
  assign RAM_DOUT_6 = RAM_DOUT;
  assign RAM_STB_5 = RAM_STB;
  assign RAM_WR_5 = RAM_WR;
endmodule

module G32_THREAD (
  input  clk,
  input  reset,
  input  en,
  input  [2:0] predicate,
  input  [3:0] alu_cmd,
  input  ldr_ram,
  input  rf_wr,
  input  [4:0] rd,
  input  [1:0] tid,
  input  alu_is_lea,
  input  alu_sel_imm,
  input  [4:0] rb,
  input  [4:0] ra,
  input  [31:0] imm,
  input  [1:0] lane_id_in,
  input  LDS_STALL,
  input  RAM_STALL,
  input  [31:0] LDS_DIN,
  input  [31:0] RAM_DIN,
  output LDS_STB,
  output RAM_STB,
  output [1:0] lane_id_out,
  output LDS_WR,
  output RAM_WR,
  output [9:0] LDS_ADDR,
  output [11:0] RAM_ADDR,
  output [31:0] LDS_DOUT,
  output [31:0] RAM_DOUT
);

  wire g32_t_condcheck_1_active, g32_t_io_1_stall_rd, g32_t_io_1_stall_wr, g32_t_rf_bank_1_pred_active,
       pull_resistor_2_node, register_1_q, register_4_q, register_5_q, register_8_q, register_9_q,
       register_13_q, register_14_q, register_15_q;
  wire [1:0] register_7_q, register_17_q;
  wire [2:0] register_2_q;
  wire [3:0] register_3_q;
  wire [4:0] register_6_q, register_16_q;
  wire [9:0] RaRb_q;
  wire [31:0] g32_t_alu_1_alu_out, g32_t_alu_ff_1_ra_3, g32_t_alu_ff_1_rb_3, g32_t_rf_bank_1_ra_2,
       g32_t_rf_bank_1_rb_2, register_10_q, register_11_q, register_12_q, register_18_q, register_19_q,
       undriven;

  Pull_Resistor pull_resistor_1 (.node(lane_id_in));
  Adder #(.width(2)) adder_1 (.a(lane_id_in), .b(2'b01), .out(lane_id_out));  // open: cin, cout
  G32_T_RF_Bank g32_t_rf_bank_1 (
    .clk(clk), .reset(reset), .wr(pull_resistor_2_node), .tid_wr(tid), .rd(register_19_q), .rb(rb), .ra(ra),
    .rd_2(register_16_q), .ra_2(g32_t_rf_bank_1_ra_2), .rb_2(g32_t_rf_bank_1_rb_2), .tid_rd(register_17_q),
    .predicate(predicate), .pred_active(g32_t_rf_bank_1_pred_active));
  // Probe on imm
  // Probe on g32_t_rf_bank_1_ra_2
  // Probe on g32_t_rf_bank_1_rb_2
  Register #(.width(1)) register_1 (.D(g32_t_rf_bank_1_pred_active), .en(en), .Q(register_1_q), .clk(clk), .clr(reset));
  // Probe on register_1_q
  Register #(.width(3)) register_2 (.D(predicate), .en(en), .Q(register_2_q), .clk(clk), .clr(reset));
  // Probe on register_2_q
  Register #(.width(4)) register_3 (.D(alu_cmd), .en(en), .Q(register_3_q), .clk(clk), .clr(reset));
  Register #(.width(10)) RaRb (.D({rb, ra}), .en(en), .Q(RaRb_q), .clk(clk), .clr(reset));
  // Probe on RaRb_q
  Register #(.width(1)) register_4 (.D(ldr_ram), .en(en), .Q(register_4_q), .clk(clk), .clr(reset));
  Register #(.width(1)) register_5 (.D(rf_wr), .en(en), .Q(register_5_q), .clk(clk), .clr(reset));
  Register #(.width(5)) register_6 (.D(rd), .en(en), .Q(register_6_q), .clk(clk), .clr(reset));
  Register #(.width(2)) register_7 (.D(tid), .en(en), .Q(register_7_q), .clk(clk), .clr(reset));
  Register #(.width(1)) register_8 (.D(alu_is_lea), .en(en), .Q(register_8_q), .clk(clk), .clr(reset));
  Register #(.width(1)) register_9 (.D(alu_sel_imm), .en(en), .Q(register_9_q), .clk(clk), .clr(reset));
  Register #(.width(32)) register_10 (.D(g32_t_rf_bank_1_ra_2), .en(en), .Q(register_10_q), .clk(clk), .clr(reset));
  Register #(.width(32)) register_11 (.D(g32_t_rf_bank_1_rb_2), .en(en), .Q(register_11_q), .clk(clk), .clr(reset));
  Register #(.width(32)) register_12 (.D(imm), .en(en), .Q(register_12_q), .clk(clk), .clr(reset));
  G32_T_CondCheck g32_t_condcheck_1 (
    .wb_dest(register_16_q), .pred_src(register_2_q), .pred_result(register_1_q),
    .active(g32_t_condcheck_1_active), .wb_d(register_19_q));
  // Probe on register_3_q
  // Probe on register_5_q
  // Probe on register_6_q
  // Probe on register_7_q
  // Probe on register_8_q
  // Probe on register_9_q
  G32_T_ALU_FF g32_t_alu_ff_1 (
    .ra(RaRb_q[4:0]), .ra_2(register_10_q), .rb(RaRb_q[9:5]), .rb_2(register_11_q), .rd_next(register_16_q),
    .rd_next_2(register_19_q), .ra_3(g32_t_alu_ff_1_ra_3), .rb_3(g32_t_alu_ff_1_rb_3));
  // Probe on register_12_q
  G32_T_ALU g32_t_alu_1 (
    .ra(g32_t_alu_ff_1_ra_3), .rb(g32_t_alu_ff_1_rb_3), .imm(register_12_q), .alu_out(g32_t_alu_1_alu_out),
    .alu_cmd(register_3_q), .alu_sel_imm(register_9_q), .alu_is_lea(register_8_q));
  // Probe on g32_t_condcheck_1_active
  // Probe on register_13_q
  Register #(.width(1)) register_13 (.D(g32_t_condcheck_1_active), .en(en), .Q(register_13_q), .clk(clk), .clr(reset));
  Register #(.width(1)) register_14 (.D(register_4_q), .en(en), .Q(register_14_q), .clk(clk), .clr(reset));
  Register #(.width(1)) register_15 (.D(register_5_q), .en(en), .Q(register_15_q), .clk(clk), .clr(reset));
  Register #(.width(5)) register_16 (.D(register_6_q), .en(en), .Q(register_16_q), .clk(clk), .clr(reset));
  Register #(.width(2)) register_17 (.D(register_7_q), .en(en), .Q(register_17_q), .clk(clk), .clr(reset));
  Register #(.width(32)) register_18 (.D(register_11_q), .en(en), .Q(register_18_q), .clk(clk), .clr(reset));
  Register #(.width(32)) register_19 (.D(g32_t_alu_1_alu_out), .en(en), .Q(register_19_q), .clk(clk), .clr(reset));
  // Probe on g32_t_alu_1_alu_out
  G32_T_IO g32_t_io_1 (
    .clk(clk), .reset(reset), .global_en(en), .en_rd(g32_t_condcheck_1_active), .en_wr(register_13_q),
    .ldr_ram_rd(register_4_q), .ldr_ram_wr(register_14_q), .addr_rd(undriven), .addr_wr(register_18_q),
    .alu_in(register_19_q), .stall_rd(g32_t_io_1_stall_rd), .stall_wr(g32_t_io_1_stall_wr),
    .LDS_STB(LDS_STB), .LDS_WR(LDS_WR), .LDS_ADDR(LDS_ADDR), .RAM_ADDR(RAM_ADDR), .LDS_STALL(LDS_STALL),
    .LDS_DIN(LDS_DIN), .LDS_DOUT(LDS_DOUT), .RAM_STB(RAM_STB), .RAM_WR(RAM_WR), .RAM_DOUT(RAM_DOUT),
    .RAM_STALL(RAM_STALL), .RAM_DIN(RAM_DIN));
  // Probe on register_15_q
  // Probe on register_16_q
  // Probe on register_17_q
  // Probe on register_18_q
  // Probe on register_19_q
  Pull_Resistor pull_resistor_2 (.node(pull_resistor_2_node));
  assign pull_resistor_2_node = register_13_q ? register_15_q : 1'bz;  // Controlled_Buffer controlled_buffer_1

  // Notes on the sheet:
  //   INSTRUCTION DECODE
  //   ADDRESSES ARE WRONG ->
  //   STALLS NOT HANDLED! ->
  //   EXECUTE / READ
  //   WRITEBACK / STORE
endmodule

module G32_T_RF_Bank (
  input  clk,
  input  reset,
  input  wr,
  input  [1:0] tid_rd,
  input  [1:0] tid_wr,
  input  [31:0] rd,
  input  [4:0] rb,
  input  [4:0] ra,
  input  [4:0] rd_2,
  input  [2:0] predicate,
  output pred_active,
  output [31:0] ra_2,
  output [31:0] rb_2
);

  wire decoder_1_out0, decoder_1_out1, decoder_1_out2, decoder_1_out3, g32_t_rf_1_pred_active,
       g32_t_rf_2_pred_active, g32_t_rf_3_pred_active, g32_t_rf_4_pred_active, g32_t_rf_ff_1_ff_d2a,
       g32_t_rf_ff_1_ff_d2b;
  wire [31:0] g32_t_rf_1_ra_2, g32_t_rf_1_rb_2, g32_t_rf_2_ra_2, g32_t_rf_2_rb_2, g32_t_rf_3_ra_2,
       g32_t_rf_3_rb_2, g32_t_rf_4_ra_2, g32_t_rf_4_rb_2, multiplexer_2_out, multiplexer_3_out;

  Decoder #(.select(2), .disabled(0)) decoder_1 (
    .out0(decoder_1_out0), .out1(decoder_1_out1), .out2(decoder_1_out2), .out3(decoder_1_out3), .sel(tid_wr),
    .en(wr));
  G32_T_RF_FF g32_t_rf_ff_1 (
    .wr(wr), .tid_rd(tid_rd), .tid_wr(tid_wr), .rb(rb), .ra(ra), .rd(rd_2), .ff_d2b(g32_t_rf_ff_1_ff_d2b),
    .ff_d2a(g32_t_rf_ff_1_ff_d2a));
  G32_T_RF g32_t_rf_1 (
    .clk(clk), .reset(reset), .wr(decoder_1_out0), .rd(rd), .rb(rb), .ra(ra), .rd_2(rd_2),
    .ra_2(g32_t_rf_1_ra_2), .rb_2(g32_t_rf_1_rb_2), .predicate(predicate),
    .pred_active(g32_t_rf_1_pred_active));
  G32_T_RF g32_t_rf_2 (
    .clk(clk), .reset(reset), .wr(decoder_1_out1), .rd(rd), .rb(rb), .ra(ra), .rd_2(rd_2),
    .ra_2(g32_t_rf_2_ra_2), .rb_2(g32_t_rf_2_rb_2), .predicate(predicate),
    .pred_active(g32_t_rf_2_pred_active));
  G32_T_RF g32_t_rf_3 (
    .clk(clk), .reset(reset), .wr(decoder_1_out2), .rd(rd), .rb(rb), .ra(ra), .rd_2(rd_2),
    .ra_2(g32_t_rf_3_ra_2), .rb_2(g32_t_rf_3_rb_2), .predicate(predicate),
    .pred_active(g32_t_rf_3_pred_active));
  G32_T_RF g32_t_rf_4 (
    .clk(clk), .reset(reset), .wr(decoder_1_out3), .rd(rd), .rb(rb), .ra(ra), .rd_2(rd_2),
    .ra_2(g32_t_rf_4_ra_2), .rb_2(g32_t_rf_4_rb_2), .predicate(predicate),
    .pred_active(g32_t_rf_4_pred_active));
  Multiplexer #(.select(2), .disabled(0), .enable("false")) multiplexer_1 (
    .in0(g32_t_rf_1_pred_active), .in1(g32_t_rf_2_pred_active), .in2(g32_t_rf_3_pred_active),
    .in3(g32_t_rf_4_pred_active), .out(pred_active), .sel(tid_rd));
  Multiplexer #(.select(2), .width(32), .disabled(0), .enable("false")) multiplexer_2 (
    .in0(g32_t_rf_1_ra_2), .in1(g32_t_rf_2_ra_2), .in2(g32_t_rf_3_ra_2), .in3(g32_t_rf_4_ra_2),
    .out(multiplexer_2_out), .sel(tid_rd));
  Multiplexer #(.select(2), .width(32), .disabled(0), .enable("false")) multiplexer_3 (
    .in0(g32_t_rf_1_rb_2), .in1(g32_t_rf_2_rb_2), .in2(g32_t_rf_3_rb_2), .in3(g32_t_rf_4_rb_2),
    .out(multiplexer_3_out), .sel(tid_rd));
  Multiplexer #(.width(32), .disabled(0), .enable("false")) multiplexer_4 (
    .in0(multiplexer_2_out), .in1(rd), .out(ra_2), .sel(g32_t_rf_ff_1_ff_d2b));
  Multiplexer #(.width(32), .disabled(0), .enable("false")) multiplexer_5 (
    .in0(multiplexer_3_out), .in1(rd), .out(rb_2), .sel(g32_t_rf_ff_1_ff_d2a));
endmodule

module G32_T_RF_FF (
  input  wr,
  input  [1:0] tid_rd,
  input  [1:0] tid_wr,
  input  [4:0] rb,
  input  [4:0] ra,
  input  [4:0] rd,
  output ff_d2b,
  output ff_d2a
);

  wire and_1_out, comparator_1_eq, comparator_2_eq, comparator_3_eq;

  Comparator #(.width(2)) comparator_1 (.a(tid_rd), .b(tid_wr), .eq(comparator_1_eq));  // open: gt, lt
  Comparator #(.width(5)) comparator_2 (.a(rb), .b(rd), .eq(comparator_2_eq));  // open: gt, lt
  Comparator #(.width(5)) comparator_3 (.a(ra), .b(rd), .eq(comparator_3_eq));  // open: gt, lt
  and and_1 (and_1_out, wr, comparator_1_eq);
  and and_2 (ff_d2b, and_1_out, comparator_2_eq);
  and and_3 (ff_d2a, and_1_out, comparator_3_eq);
endmodule

module G32_T_RF (
  input  clk,
  input  reset,
  input  wr,
  input  [2:0] predicate,
  input  [31:0] rd,
  input  [4:0] rb,
  input  [4:0] ra,
  input  [4:0] rd_2,
  output pred_active,
  output [31:0] ra_2,
  output [31:0] rb_2
);

  wire comparator_1_eq, decoder_1_out0, decoder_1_out1, decoder_1_out2, decoder_1_out3, decoder_1_out4,
       decoder_1_out5, decoder_1_out6, decoder_1_out7, decoder_1_out8, decoder_1_out9, decoder_1_out10,
       decoder_1_out11, decoder_1_out12, decoder_1_out13, decoder_1_out14, decoder_1_out15, decoder_1_out16,
       decoder_1_out17, decoder_1_out18, decoder_1_out19, decoder_1_out20, decoder_1_out21, decoder_1_out22,
       decoder_1_out23, decoder_1_out24, decoder_1_out25, decoder_1_out26, decoder_1_out27, decoder_1_out28,
       decoder_1_out29, decoder_1_out30, decoder_1_out31, pull_resistor_1_node;
  wire [31:0] multiplexer_1_out, pull_resistor_2_node, register_1_q, register_2_q, register_3_q,
       register_4_q, register_5_q, register_6_q, register_7_q, register_8_q, register_9_q, register_10_q,
       register_11_q, register_12_q, register_13_q, register_14_q, register_15_q, register_16_q,
       register_17_q, register_18_q, register_19_q, register_20_q, register_21_q, register_22_q,
       register_23_q, register_24_q, register_25_q, register_26_q, register_27_q, register_28_q,
       register_29_q, register_30_q, register_31_q, register_32_q;

  Decoder #(.select(5), .disabled(0)) decoder_1 (
    .out0(decoder_1_out0), .out1(decoder_1_out1), .out2(decoder_1_out2), .out3(decoder_1_out3),
    .out4(decoder_1_out4), .out5(decoder_1_out5), .out6(decoder_1_out6), .out7(decoder_1_out7),
    .out8(decoder_1_out8), .out9(decoder_1_out9), .out10(decoder_1_out10), .out11(decoder_1_out11),
    .out12(decoder_1_out12), .out13(decoder_1_out13), .out14(decoder_1_out14), .out15(decoder_1_out15),
    .out16(decoder_1_out16), .out17(decoder_1_out17), .out18(decoder_1_out18), .out19(decoder_1_out19),
    .out20(decoder_1_out20), .out21(decoder_1_out21), .out22(decoder_1_out22), .out23(decoder_1_out23),
    .out24(decoder_1_out24), .out25(decoder_1_out25), .out26(decoder_1_out26), .out27(decoder_1_out27),
    .out28(decoder_1_out28), .out29(decoder_1_out29), .out30(decoder_1_out30), .out31(decoder_1_out31),
    .sel(rd_2), .en(wr));
  Pull_Resistor pull_resistor_1 (.node(pull_resistor_1_node));
  Register #(.width(32)) register_1 (.D(rd), .en(pull_resistor_1_node), .Q(register_1_q), .clk(clk), .clr(reset));
  Register #(.width(32)) register_2 (.D(rd), .en(decoder_1_out1), .Q(register_2_q), .clk(clk), .clr(reset));
  Register #(.width(32)) register_3 (.D(rd), .en(decoder_1_out2), .Q(register_3_q), .clk(clk), .clr(reset));
  Register #(.width(32)) register_4 (.D(rd), .en(decoder_1_out3), .Q(register_4_q), .clk(clk), .clr(reset));
  Register #(.width(32)) register_5 (.D(rd), .en(decoder_1_out4), .Q(register_5_q), .clk(clk), .clr(reset));
  Register #(.width(32)) register_6 (.D(rd), .en(decoder_1_out5), .Q(register_6_q), .clk(clk), .clr(reset));
  Register #(.width(32)) register_7 (.D(rd), .en(decoder_1_out6), .Q(register_7_q), .clk(clk), .clr(reset));
  Register #(.width(32)) register_8 (.D(rd), .en(decoder_1_out7), .Q(register_8_q), .clk(clk), .clr(reset));
  Register #(.width(32)) register_9 (.D(rd), .en(decoder_1_out8), .Q(register_9_q), .clk(clk), .clr(reset));
  Register #(.width(32)) register_10 (.D(rd), .en(decoder_1_out9), .Q(register_10_q), .clk(clk), .clr(reset));
  Register #(.width(32)) register_11 (.D(rd), .en(decoder_1_out10), .Q(register_11_q), .clk(clk), .clr(reset));
  Register #(.width(32)) register_12 (.D(rd), .en(decoder_1_out11), .Q(register_12_q), .clk(clk), .clr(reset));
  Register #(.width(32)) register_13 (.D(rd), .en(decoder_1_out12), .Q(register_13_q), .clk(clk), .clr(reset));
  Register #(.width(32)) register_14 (.D(rd), .en(decoder_1_out13), .Q(register_14_q), .clk(clk), .clr(reset));
  Register #(.width(32)) register_15 (.D(rd), .en(decoder_1_out14), .Q(register_15_q), .clk(clk), .clr(reset));
  Register #(.width(32)) register_16 (.D(rd), .en(decoder_1_out15), .Q(register_16_q), .clk(clk), .clr(reset));
  Register #(.width(32)) register_17 (.D(rd), .en(decoder_1_out16), .Q(register_17_q), .clk(clk), .clr(reset));
  Register #(.width(32)) register_18 (.D(rd), .en(decoder_1_out17), .Q(register_18_q), .clk(clk), .clr(reset));
  Register #(.width(32)) register_19 (.D(rd), .en(decoder_1_out18), .Q(register_19_q), .clk(clk), .clr(reset));
  Register #(.width(32)) register_20 (.D(rd), .en(decoder_1_out19), .Q(register_20_q), .clk(clk), .clr(reset));
  Register #(.width(32)) register_21 (.D(rd), .en(decoder_1_out20), .Q(register_21_q), .clk(clk), .clr(reset));
  Register #(.width(32)) register_22 (.D(rd), .en(decoder_1_out21), .Q(register_22_q), .clk(clk), .clr(reset));
  Register #(.width(32)) register_23 (.D(rd), .en(decoder_1_out22), .Q(register_23_q), .clk(clk), .clr(reset));
  Register #(.width(32)) register_24 (.D(rd), .en(decoder_1_out23), .Q(register_24_q), .clk(clk), .clr(reset));
  Register #(.width(32)) register_25 (.D(rd), .en(decoder_1_out24), .Q(register_25_q), .clk(clk), .clr(reset));
  Register #(.width(32)) register_26 (.D(rd), .en(decoder_1_out25), .Q(register_26_q), .clk(clk), .clr(reset));
  Register #(.width(32)) register_27 (.D(rd), .en(decoder_1_out26), .Q(register_27_q), .clk(clk), .clr(reset));
  Register #(.width(32)) register_28 (.D(rd), .en(decoder_1_out27), .Q(register_28_q), .clk(clk), .clr(reset));
  Register #(.width(32)) register_29 (.D(rd), .en(decoder_1_out28), .Q(register_29_q), .clk(clk), .clr(reset));
  Register #(.width(32)) register_30 (.D(rd), .en(decoder_1_out29), .Q(register_30_q), .clk(clk), .clr(reset));
  Register #(.width(32)) register_31 (.D(rd), .en(decoder_1_out30), .Q(register_31_q), .clk(clk), .clr(reset));
  Register #(.width(32)) register_32 (.D(rd), .en(decoder_1_out31), .Q(register_32_q), .clk(clk), .clr(reset));
  Pull_Resistor pull_resistor_2 (.node(pull_resistor_2_node));
  Multiplexer #(.select(2), .width(32), .enable("false")) multiplexer_1 (
    .in0(register_1_q), .in1(register_3_q), .in2(register_4_q), .in3(register_5_q), .out(multiplexer_1_out),
    .sel(predicate[1:0]));
  Comparator #(.width(32)) comparator_1 (
    .a(pull_resistor_2_node), .b(multiplexer_1_out), .eq(comparator_1_eq));  // open: gt, lt
  xor xor_1 (pred_active, predicate[2], comparator_1_eq);
  Multiplexer #(.select(5), .width(32), .enable("false")) multiplexer_2 (
    .in0(register_1_q), .in1(register_2_q), .in2(register_3_q), .in3(register_4_q), .in4(register_5_q),
    .in5(register_6_q), .in6(register_7_q), .in7(register_8_q), .in8(register_9_q), .in9(register_10_q),
    .in10(register_11_q), .in11(register_12_q), .in12(register_13_q), .in13(register_14_q),
    .in14(register_15_q), .in15(register_16_q), .in16(register_17_q), .in17(register_18_q),
    .in18(register_19_q), .in19(register_20_q), .in20(register_21_q), .in21(register_22_q),
    .in22(register_23_q), .in23(register_24_q), .in24(register_25_q), .in25(register_26_q),
    .in26(register_27_q), .in27(register_28_q), .in28(register_29_q), .in29(register_30_q),
    .in30(register_31_q), .in31(register_32_q), .out(rb_2), .sel(rb));
  Multiplexer #(.select(5), .width(32), .enable("false")) multiplexer_3 (
    .in0(register_1_q), .in1(register_2_q), .in2(register_3_q), .in3(register_4_q), .in4(register_5_q),
    .in5(register_6_q), .in6(register_7_q), .in7(register_8_q), .in8(register_9_q), .in9(register_10_q),
    .in10(register_11_q), .in11(register_12_q), .in12(register_13_q), .in13(register_14_q),
    .in14(register_15_q), .in15(register_16_q), .in16(register_17_q), .in17(register_18_q),
    .in18(register_19_q), .in19(register_20_q), .in20(register_21_q), .in21(register_22_q),
    .in22(register_23_q), .in23(register_24_q), .in24(register_25_q), .in25(register_26_q),
    .in26(register_27_q), .in27(register_28_q), .in28(register_29_q), .in29(register_30_q),
    .in30(register_31_q), .in31(register_32_q), .out(ra_2), .sel(ra));
endmodule

module G32_T_ALU (
  input  alu_is_lea,
  input  [3:0] alu_cmd,
  input  alu_sel_imm,
  input  [31:0] ra,
  input  [31:0] rb,
  input  [31:0] imm,
  output [31:0] alu_out
);

  wire adder_1_cout;
  wire [31:0] adder_1_out, adder_2_out, and_1_out, divider_1_out, multiplexer_1_out, multiplier_1_out,
       or_1_out, pull_resistor_1_node, pull_resistor_2_node, pull_resistor_3_node, pull_resistor_4_node,
       pull_resistor_5_node, pull_resistor_6_node, pull_resistor_7_node, pull_resistor_8_node, shifter_1_out,
       shifter_2_out, shifter_3_out, subtractor_1_out, xor_1_out;

  Multiplexer #(.width(32), .disabled(0), .enable("false")) multiplexer_1 (
    .in0(rb), .in1(imm), .out(multiplexer_1_out), .sel(alu_sel_imm));
  Adder #(.width(32)) adder_1 (.out(adder_1_out), .cout(adder_1_cout));  // open: a, b, cin
  Pull_Resistor #(.pull(1)) pull_resistor_1 (.node(pull_resistor_1_node));
  BitFinder bitfinder_1 ();  // open: in, index, found
  Multiplexer #(.width(32), .disabled(0), .enable("false")) multiplexer_2 (
    .in0(adder_1_out), .in1(pull_resistor_1_node), .sel(adder_1_cout));  // open: out
  Pull_Resistor pull_resistor_2 (.node(pull_resistor_2_node));
  Comparator #(.width(32)) comparator_1 (.a(pull_resistor_2_node));  // open: b, gt, eq, lt
  Adder #(.width(32)) adder_2 (.a(ra), .b(multiplexer_1_out), .out(adder_2_out));  // open: cin, cout
  Multiplier #(.width(32)) multiplier_1 (.a(ra), .b(multiplexer_1_out), .out(multiplier_1_out));  // open: cin, cout
  Pull_Resistor #(.pull("X")) pull_resistor_3 (.node(pull_resistor_3_node));
  assign and_1_out = ra & multiplexer_1_out;  // AND_Gate and_1, 32 bits wide
  assign or_1_out = ra | multiplexer_1_out;  // OR_Gate or_1, 32 bits wide
  Shifter #(.width(32)) shifter_1 (.in(ra), .\dist (multiplexer_1_out[4:0]), .out(shifter_1_out));
  Shifter #(.width(32), .shift("lr")) shifter_2 (.in(ra), .\dist (multiplexer_1_out[4:0]), .out(shifter_2_out));
  Shifter #(.width(32), .shift("ar")) shifter_3 (.in(ra), .\dist (multiplexer_1_out[4:0]), .out(shifter_3_out));
  Subtractor #(.width(32)) subtractor_1 (.a(ra), .b(multiplexer_1_out), .out(subtractor_1_out));  // open: bin, bout
  Divider #(.width(32)) divider_1 (.a(ra), .b(multiplexer_1_out), .out(divider_1_out));  // open: upper, rem
  Pull_Resistor #(.pull("X")) pull_resistor_4 (.node(pull_resistor_4_node));
  assign xor_1_out = ra ^ multiplexer_1_out;  // XOR_Gate xor_1, 32 bits wide
  Pull_Resistor #(.pull("X")) pull_resistor_5 (.node(pull_resistor_5_node));
  Pull_Resistor #(.pull("X")) pull_resistor_6 (.node(pull_resistor_6_node));
  Pull_Resistor #(.pull("X")) pull_resistor_7 (.node(pull_resistor_7_node));
  Pull_Resistor #(.pull("X")) pull_resistor_8 (.node(pull_resistor_8_node));
  Multiplexer #(.select(4), .width(32), .enable("false")) multiplexer_3 (
    .in0(adder_2_out), .in1(multiplier_1_out), .in2(pull_resistor_3_node), .in3(and_1_out), .in4(or_1_out),
    .in5(shifter_1_out), .in6(shifter_2_out), .in7(shifter_3_out), .in8(subtractor_1_out),
    .in9(divider_1_out), .in10(pull_resistor_4_node), .in11(xor_1_out), .in12(pull_resistor_5_node),
    .in13(pull_resistor_6_node), .in14(pull_resistor_7_node), .in15(pull_resistor_8_node), .out(alu_out),
    .sel(alu_cmd));
endmodule

module G32_T_ALU_FF (
  input  [4:0] ra,
  input  [31:0] ra_2,
  input  [4:0] rb,
  input  [31:0] rb_2,
  input  [4:0] rd_next,
  input  [31:0] rd_next_2,
  output [31:0] ra_3,
  output [31:0] rb_3
);

  wire comparator_1_eq, comparator_2_eq;

  Comparator #(.width(5)) comparator_1 (.a(ra), .b(rd_next), .eq(comparator_1_eq));  // open: gt, lt
  Multiplexer #(.width(32), .disabled(0), .enable("false")) multiplexer_1 (
    .in0(ra_2), .in1(rd_next_2), .out(ra_3), .sel(comparator_1_eq));
  Comparator #(.width(5)) comparator_2 (.a(rb), .b(rd_next), .eq(comparator_2_eq));  // open: gt, lt
  Multiplexer #(.width(32), .disabled(0), .enable("false")) multiplexer_2 (
    .in0(rb_2), .in1(rd_next_2), .out(rb_3), .sel(comparator_2_eq));
endmodule

module G32_T_CondCheck (
  input  [2:0] pred_src,
  input  [4:0] wb_dest,
  input  pred_result,
  input  [31:0] wb_d,
  output active
);

  wire and_1_out, comparator_1_eq, comparator_2_eq, comparator_3_eq, xor_1_out;
  wire [1:0] pull_resistor_1_node;
  wire [31:0] pull_resistor_2_node;

  Comparator #(.width(2)) comparator_1 (.a(pred_src[1:0]), .b(wb_dest[1:0]), .eq(comparator_1_eq));  // open: gt, lt
  Comparator #(.width(2)) comparator_2 (
    .a(wb_dest[4:3]), .b(pull_resistor_1_node), .eq(comparator_2_eq));  // open: gt, lt
  Pull_Resistor pull_resistor_1 (.node(pull_resistor_1_node));
  Comparator #(.width(32)) comparator_3 (.a(wb_d), .b(pull_resistor_2_node), .eq(comparator_3_eq));  // open: gt, lt
  Pull_Resistor pull_resistor_2 (.node(pull_resistor_2_node));
  and and_1 (and_1_out, comparator_1_eq, comparator_2_eq);
  xor xor_1 (xor_1_out, wb_dest[2], comparator_3_eq);
  Multiplexer #(.disabled(0), .enable("false")) multiplexer_1 (
    .in0(pred_result), .in1(xor_1_out), .out(active), .sel(and_1_out));
endmodule

module G32_T_Flags (
  input  clk,
  input  reset,
  input  en,
  input  [2:0] flag_update_mask,
  input  [2:0] condition,
  output [2:0] condition_2
);

  wire [2:0] controlled_buffer_1_out;

  assign controlled_buffer_1_out = en ? flag_update_mask : 3'bz;  // Controlled_Buffer controlled_buffer_1
  Pull_Resistor pull_resistor_1 (.node(controlled_buffer_1_out));
  Register #(.width(1)) register_1 (
    .D(condition[0]), .en(controlled_buffer_1_out[0]), .Q(condition_2[0]), .clk(clk), .clr(reset));
  Register #(.width(1)) register_2 (
    .D(condition[1]), .en(controlled_buffer_1_out[1]), .Q(condition_2[1]), .clk(clk), .clr(reset));
  Register #(.width(1)) register_3 (
    .D(condition[2]), .en(controlled_buffer_1_out[2]), .Q(condition_2[2]), .clk(clk), .clr(reset));
endmodule

module G32_T_IO (
  input  clk,
  input  reset,
  input  global_en,
  input  en_rd,
  input  en_wr,
  input  LDS_STB,
  input  ldr_ram_rd,
  input  LDS_WR,
  input  ldr_ram_wr,
  input  [31:0] addr_rd,
  input  [9:0] LDS_ADDR,
  input  [11:0] RAM_ADDR,
  input  [31:0] addr_wr,
  input  [31:0] LDS_DOUT,
  input  RAM_STB,
  input  [31:0] alu_in,
  input  RAM_WR,
  input  [31:0] RAM_DOUT,
  input  [31:0] RAM_DIN,
  output stall_rd,
  output stall_wr,
  output LDS_STALL,
  output [31:0] LDS_DIN,
  output RAM_STALL
);

  wire and_1_out, not_1_out, or_1_out, or_2_out;
  wire [11:0] demultiplexer_1_out0, demultiplexer_1_out1, demultiplexer_2_out0, demultiplexer_2_out1;

  and and_1 (and_1_out, global_en, or_1_out);
  or or_1 (or_1_out, en_rd, en_wr);
  Demultiplexer #(.width(12), .disabled(0), .enable("false")) demultiplexer_1 (
    .out0(demultiplexer_1_out0), .out1(demultiplexer_1_out1), .in(addr_rd[11:0]), .sel(ldr_ram_rd));
  Demultiplexer #(.width(12), .disabled(0), .enable("false")) demultiplexer_2 (
    .out0(demultiplexer_2_out0), .out1(demultiplexer_2_out1), .in(addr_wr[11:0]), .sel(ldr_ram_wr));
  or or_2 (or_2_out, and_1_out, en_wr);
  not not_1 (not_1_out, ldr_ram_rd);
  and and_2 (LDS_STB, or_2_out, not_1_out);
  and and_3 (RAM_STB, or_2_out, ldr_ram_rd);
  Pull_Resistor pull_resistor_1 ();  // open: node
  Controlled_Buffer #(.width(32)) controlled_buffer_1 ();  // open: in, out, en
  Pull_Resistor #(.pull("X")) pull_resistor_2 (.node(stall_rd));
  Pull_Resistor #(.pull("X")) pull_resistor_3 (.node(stall_wr));

  assign LDS_DOUT = alu_in;
  assign LDS_WR = en_wr;
  assign RAM_ADDR[9:0] = LDS_ADDR;
  assign RAM_DOUT = alu_in;
  assign RAM_WR = en_wr;
endmodule
